// Digital circuit comparator_4bit.dig as structural Verilog
module comparator_4bit (
  input  [3:0] A,
  input  [3:0] B,
  output Greater,
  output Equal,
  output Less
);

  Comparator #(.Bits(4)) comparator_1 (.a(A), .b(B), .gt(Greater), .eq(Equal), .lt(Less));
endmodule
