// Digital circuit five_inputand.dig as structural Verilog
module five_inputand (
  input  in_1,
  input  in_2,
  input  in_3,
  input  in_4,
  input  in_5,
  output out_6
);

  and and_1 (out_6, in_1, in_2, in_3, in_4, in_5);
endmodule
