// Digital circuit mux_2to1.dig as structural Verilog
module mux_2to1 (
  input  In0,
  input  In1,
  input  Sel,
  output Y
);

  Multiplexer multiplexer_1 (.sel(Sel), .in_0(In0), .in_1(In1), .out(Y));
endmodule
