// Digital circuit register_test.dig as structural Verilog
module register_test (
  input  [3:0] D,
  input  clk,
  output [3:0] Q
);

  Register #(.Bits(4)) register_1 (.D(D), .C(clk), .en(1'b1), .Q(Q));
endmodule
