// Digital circuit six_inputand.dig as structural Verilog
module six_inputand (
  input  in_1,
  input  in_2,
  input  in_3,
  input  in_4,
  input  in_5,
  input  in_6,
  output out_7
);

  and and_1 (out_7, in_4, in_3, in_1, in_2, in_5, in_6);
endmodule
