// Digital circuit splitter_test.dig as structural Verilog
module splitter_test (
  input  [3:0] Bus,
  output b0,
  output b1,
  output b2,
  output b3
);


  assign b0 = Bus[0];
  assign b1 = Bus[1];
  assign b2 = Bus[2];
  assign b3 = Bus[3];
endmodule
