// Digital circuit two_subcircuits.dig as structural Verilog
module two_subcircuits (
  input  P,
  input  Q,
  input  R,
  output Y
);

  wire subcircuit_inner_1_p3, subcircuit_inner_2_p3;

  // subcircuit_inner subcircuit_inner_1: pin names not known; wires that end beside it: P, Q, subcircuit_inner_1_p3
  // subcircuit_inner subcircuit_inner_2: pin names not known; wires that end beside it: P, R, subcircuit_inner_2_p3
  and and_1 (Y, subcircuit_inner_1_p3, subcircuit_inner_2_p3);
endmodule
