// Digital circuit uses_subcircuit.dig as structural Verilog
module uses_subcircuit (
  input  X,
  input  Z,
  output Out
);

  // subcircuit_inner subcircuit_inner_1: pin names not known; wires that end beside it: X, Z, Out
endmodule
